# Fritzing sketch Microphone (saved by Fritzing 0.9.3b)
breadboards: 1

parts:
  Uno = Arduino Uno (Rev3)
  Микрофон = Breakout Board for Electret Microphone
  LED1 = LED - 5mm [color="Yellow (595nm)" package="5 mm [THT]"]
  LED2 = LED - 5mm [color="White (4500K)" package="5 mm [THT]"]
  LED3 = LED - 5mm [color="Green (560nm)" package="5 mm [THT]"]
  R1 = Resistor [tolerance=±5% resistance=220 package="2010 [SMD]"]
  R2 = Resistor [tolerance=±5% resistance=220 package="2010 [SMD]"]
  R3 = Resistor [tolerance=±5% resistance=220 package="2010 [SMD]"]

nets:
  N1: Uno.A5/SCL, Микрофон.AUD
  N2: Uno.D9_PWM, R3.Pin_0
  N3: Uno.D11_PWM/MOSI, R2.Pin_0
  N4: Uno.D13/SCK, R1.Pin_0
  GND: Uno.GND, Микрофон.GND, LED1.cathode, LED2.cathode, LED3.cathode
  5V: Uno.5V, Микрофон.VCC
  N5: LED1.anode, R1.Pin_1
  N6: LED2.anode, R2.Pin_1
  N7: LED3.anode, R3.Pin_1
